# Fritzing sketch ESP32_Demo (saved by Fritzing 0.9.4)
circuit board: 8.46667cm x 5.64444cm
breadboards: 2

parts:
  Part1 = AZ-Delivery ESP32 Dev Kit C V2 [part_number="AZ-Delivery ESP Dev Kit C V2"]
  LED1 = RGB LED (com. cathode, rgb) [package="5 mm [THT]"]
  LED2 = LED - 5mm [color="Red (633nm)" package="5 mm [THT]"]
  LCD1 = LCD screen
  R5 = Rotary Potentiometer (Small) [maximum_resistance=100kΩ package=THT]
  S1 = Pushbutton [package="[THT]"]
  R6 = Photocell (LDR) [package=THT]
  R7 = Resistor [tolerance=±5% resistance=220 package=THT]  # not connected
  R8 = Resistor [tolerance=±5% resistance=100 package=THT]  # not connected
  R9 = Resistor [tolerance=±5% resistance=100 package=THT]  # not connected
  R10 = Resistor [tolerance=±5% resistance=10k package=THT]
  R11 = Resistor [tolerance=±5% resistance=10k package=THT]
  R4 = Resistor [tolerance=±5% resistance=100 package=THT]
  R3 = Resistor [tolerance=±5% resistance=220 package=THT]
  R2 = Resistor [tolerance=±5% resistance=220 package=THT]
  R1 = Resistor [tolerance=±5% resistance=220 package=THT]
  RHT1 = Humidity and Temperature Sensor RHT03
  IR1 = TSOP312.., 314.. [package=THT]

nets:
  3V3: Part1.3V3, LCD1.LED-, R5.leg1, S1.Pin_1, S1.Pin_2, R6.pin_1, RHT1.Vcc, IR1.Vs
  N1: Part1.G34, S1.Pin_3, S1.Pin_4, R11.Pin_1
  N2: Part1.G35, IR1.Data
  N3: Part1.G32, RHT1.Data-signal
  N4: Part1.G33, R6.pin_0, R10.Pin_1
  VSS: Part1.GND#13, Part1.GND#31, Part1.GND#37, LED1.common_cathode, LED2.cathode, LCD1.VSS, LCD1.R/W, LCD1.LED+, R5.leg2, R10.Pin_0, R11.Pin_0, RHT1.GND_1, IR1.GND
  N5: Part1.V5, LCD1.VDD
  N6: Part1.G15, R1.Pin_0
  N7: Part1.G2, R2.Pin_0
  N8: Part1.G0, R3.Pin_0
  N9: Part1.G4, R4.Pin_0
  N10: Part1.G5, LCD1.DB4
  N11: Part1.G18, LCD1.DB5
  N12: Part1.G19, LCD1.DB6
  N13: Part1.G21, LCD1.DB7
  N14: Part1.G22, LCD1.RS
  N15: Part1.G23, LCD1.E
  N16: LED1.red_anode, LED1.blue_anode, R3.Pin_1, R1.Pin_1
  N17: LED1.green_anode, R2.Pin_1
  N18: LED2.anode, R4.Pin_1

custom parts:
  AZ-Delivery ESP32 Dev Kit C V2: Based on the part by Stephen Lilley for the HiLetgo ESP-WROOM-32 ESP32 ESP-32S Development Board 2.4GHz Dual-Mode WiFi + Bluetooth Dual Cores Microcontroller
